# Fritzing sketch Serial controller (saved by Fritzing 0.9.3b)
circuit board: 8.2cm x 5.9cm
breadboards: 1

parts:
  DBUS = DB9 Connector [package=db9]
  C5 = Capacitor [package=0603-cap]
  C6 = Capacitor [package=0603-cap]
  C3 = Capacitor [package=0603-cap]
  C4 = Capacitor [package=0603-cap]
  C7 = Capacitor [package=0603-cap]
  J1 = Power Jack [package=power_jack_pth_lock]
  328PU = atmega328 [package=dip]
  LED1 = smd LED [color="Green (570nm)" package="0603 [SMD]"]
  J1_2 = Resistor [tolerance=±5% resistance=150 package="0603 [SMD]"]
  LED2 = smd LED [color="Green (570nm)" package="0603 [SMD]"]
  J2 = Resistor [tolerance=±5% resistance=150 package="0603 [SMD]"]
  LED3 = smd LED [color="Green (570nm)" package="0603 [SMD]"]
  J3 = Resistor [tolerance=±5% resistance=150 package="0603 [SMD]"]
  LED4 = smd LED [color="Green (570nm)" package="0603 [SMD]"]
  J4 = Resistor [tolerance=±5% resistance=150 package="0603 [SMD]"]
  LED5 = smd LED [color="Green (570nm)" package="0603 [SMD]"]
  J5 = Resistor [tolerance=±5% resistance=220 package="0603 [SMD]"]
  LED6 = smd LED [color="Green (570nm)" package="0603 [SMD]"]
  J6 = Resistor [tolerance=±5% resistance=150 package="0603 [SMD]"]
  LED7 = smd LED [color="Green (570nm)" package="0603 [SMD]"]
  J7 = Resistor [tolerance=±5% resistance=220 package="0603 [SMD]"]
  J8 = Resistor [tolerance=±5% resistance=150 package="0603 [SMD]"]
  LED8 = smd LED [color="Green (570nm)" package="0603 [SMD]"]
  16MHz = Crystal [frequency="16 Mhz" package=SMD]
  7805 = Voltage Regulator - 5V [package="DPak [SMD]"]
  S1 = Toggle Switch [package=THT]
  PWR = smd LED [color="Green (570nm)" package="0603 [SMD]"]
  R9 = Resistor [tolerance=±5% resistance=150 package="0603 [SMD]"]
  ULN2803 = Darlington Driver [package=so18l]
  STATUS = smd LED [color="Green (570nm)" package="0603 [SMD]"]
  R10 = Resistor [tolerance=±5% resistance=220 package="0603 [SMD]"]
  J2_2 = double row male pin header, 16 pins [form="♂ (male)"]
  U7 = 9007 Reed relay [package=THT]
  U2 = 9007 Reed relay [package=THT]
  U6 = 9007 Reed relay [package=THT]
  U5 = 9007 Reed relay [package=THT]
  U1 = 9007 Reed relay [package=THT]
  U8 = 9007 Reed relay [package=THT]
  U4 = 9007 Reed relay [package=THT]
  U3 = 9007 Reed relay [package=THT]
  MAX232 = RS232 Transceiver [package=dil16]
  C1 = Capacitor [package=0603-cap]
  C2 = Capacitor [package=0603-cap]

nets:
  N1: DBUS.2, MAX232.T1OUT
  N2: DBUS.3, MAX232.R1IN
  GND: DBUS.5, C5.1, C6.1, C7.2, J1.GND, J1.GNDBREAK, 328PU.GND, 7805.GND, R9.Pin_0, ULN2803.9, STATUS.cathode, MAX232.GND, C1.1, C2.1
  N3: C5.2, MAX232.V+
  N4: C6.2, MAX232.V-
  N5: C3.1, MAX232.C1+
  N6: C3.2, MAX232.C1-
  N7: C4.1, MAX232.C2-
  N8: C4.2, MAX232.C2+
  VCC: C7.1, 328PU.VCC, LED1.anode, LED2.anode, LED3.anode, LED4.anode, LED5.anode, LED6.anode, LED7.anode, LED8.anode, 7805.output_voltage, PWR.anode, ULN2803.10, U7.COIL_+, U2.COIL_+, U6.COIL_+, U5.COIL_+, U1.COIL_+, U8.COIL_+, U4.COIL_+, U3.COIL_+, MAX232.VCC
  N9: J1.PWR, S1.COM
  N10: 328PU.D2, ULN2803.8
  N11: 328PU.D3_(PWM), ULN2803.7
  N12: 328PU.D4, ULN2803.6
  N13: 328PU.XLAT1, 16MHz.pin_0, C1.2
  N14: 328PU.XLAT2, 16MHz.pin_1, C2.2
  N15: 328PU.D5_(PWM), ULN2803.5
  N16: 328PU.D6_(PWM), ULN2803.4
  N17: 328PU.D7, ULN2803.3
  N18: 328PU.D8, ULN2803.2
  N19: 328PU.D9_(PWM), ULN2803.1
  N20: 328PU.D10_(PWM), MAX232.T1IN
  N21: 328PU.D11_(PWM), MAX232.R1OUT
  N22: 328PU.D12, R10.Pin_1
  N23: LED1.cathode, J1_2.Pin_1
  N24: J1_2.Pin_0, ULN2803.18, U1.COIL_-
  N25: LED2.cathode, J2.Pin_1
  N26: J2.Pin_0, ULN2803.17, U2.COIL_-
  N27: LED3.cathode, J3.Pin_1
  N28: J3.Pin_0, ULN2803.16, U3.COIL_-
  N29: LED4.cathode, J4.Pin_1
  N30: J4.Pin_0, ULN2803.15, U4.COIL_-
  N31: LED5.cathode, J5.Pin_1
  N32: J5.Pin_0, ULN2803.14, U5.COIL_-
  N33: LED6.cathode, J6.Pin_1
  N34: J6.Pin_0, ULN2803.13, U6.COIL_-
  N35: LED7.cathode, J7.Pin_1
  N36: J7.Pin_0, ULN2803.12, U7.COIL_-
  N37: J8.Pin_0, ULN2803.11, U8.COIL_-
  N38: J8.Pin_1, LED8.cathode
  N39: 7805.input_voltage, S1.L1
  N40: PWR.cathode, R9.Pin_1
  N41: STATUS.anode, R10.Pin_0
  N42: J2_2.pin1, U1.NO
  N43: J2_2.pin2, U2.NO
  N44: J2_2.pin3, U3.NO
  N45: J2_2.pin4, U4.NO
  N46: J2_2.pin5, U5.MAIN
  N47: J2_2.pin6, U6.MAIN
  N48: J2_2.pin7, U7.MAIN
  N49: J2_2.pin8, U8.MAIN
  N50: J2_2.pin9, U8.NO
  N51: J2_2.pin10, U7.NO
  N52: J2_2.pin11, U6.NO
  N53: J2_2.pin12, U5.NO
  N54: J2_2.pin13, U4.MAIN
  N55: J2_2.pin14, U3.MAIN
  N56: J2_2.pin15, U2.MAIN
  N57: J2_2.pin16, U1.MAIN

notes:
  Serial relay controller
  Michael Tao
  Serial Controlled
  Relay board
  Michael Tao
  7/25/2018

custom parts:
  9007 Reed relay: Coto Technology SPST Reed relay with diode protection pin 2 + pin 3 -
